# Fritzing sketch wlanthermo_easy (saved by Fritzing 0.9.4)
stripboards: 2

parts:
  R4 = Resistor [tolerance=±20% resistance=47k package=THT]
  U4 = 2.5mm Audio Jack [package=stereojack2.5mm_smd]
  R6 = Resistor [tolerance=±20% resistance=47k package=THT]
  U5 = 2.5mm Audio Jack [package=stereojack2.5mm_smd]
  R8 = Resistor [tolerance=±20% resistance=47k package=THT]
  Squix1 = OLED 0.96" 128x64 I2C SSD1306
  IC1 = LM4040 [package=to-92]
  MCP1 = MCP3208
  U2 = 2.5mm Audio Jack [package=stereojack2.5mm_smd]
  C4 = Film/Foil Capacitor [capacitance=100nF voltage=35V package="5mm [THT, pp]"]
  C3 = Film/Foil Capacitor [capacitance=100nF voltage=35V package="5mm [THT, pp]"]
  C2 = Film/Foil Capacitor [capacitance=100nF voltage=35V package="5mm [THT, pp]"]
  C6 = Film/Foil Capacitor [capacitance=100nF voltage=35V package="5mm [THT, pp]"]
  C5 = Film/Foil Capacitor [capacitance=100nF voltage=35V package="5mm [THT, pp]"]
  U3 = 2.5mm Audio Jack [package=stereojack2.5mm_smd]
  R12 = Resistor [tolerance=±20% resistance=10k package=THT]
  R13 = Resistor [tolerance=±20% resistance=10k package=THT]
  R14 = Vertical Resistor [tolerance=±5% resistance=2.32k package=THT]
  C7 = Film/Foil Capacitor [capacitance=100nF voltage=35V package="5mm [THT, pp]"]
  C1 = Film/Foil Capacitor [capacitance=100nF voltage=35V package="5mm [THT, pp]"]
  R1 = Vertical Resistor [tolerance=±5% resistance=1k package=THT]
  R2 = Resistor [tolerance=±20% resistance=47k package=THT]
  R3 = Vertical Resistor [tolerance=±5% resistance=1k package=THT]
  R5 = Vertical Resistor [tolerance=±5% resistance=1k package=THT]
  R7 = Vertical Resistor [tolerance=±5% resistance=1k package=THT]
  R15 = Resistor [tolerance=±20% resistance=10k package=THT]
  R16 = Resistor [tolerance=±20% resistance=10k package=THT]
  S1 = Pushbutton [package=THT]
  S2 = Pushbutton [package=THT]
  U1 = NodeMCU V1.0

nets:
  VRef: R4.Pin_0, R6.Pin_0, R8.Pin_0, IC1.+, MCP1.VREF, R14.Pin_1, C7.-, R2.Pin_0
  N1: R4.Pin_1, U3.LEFT, R3.Pin_0
  N2: U4.LEFT, R6.Pin_1, R5.Pin_0
  CH12: U4.RIGHT
  GND: U4.SLEEVE, U5.SLEEVE, Squix1.GND, IC1.-, MCP1.DGND, MCP1.AGND, U2.SLEEVE, C4.-, C3.-, C2.-, C6.+, C5.+, U3.SLEEVE, C7.+, C1.-, S1.leg0, S2.leg1, U1.GND
  N3: U5.LEFT, R8.Pin_1, R7.Pin_0
  CH11: U5.RIGHT
  3.3V: Squix1.VCC, MCP1.VDD, C6.-, C5.-, R12.Pin_1, R13.Pin_1, R14.Pin_0, R15.Pin_1, R16.Pin_1, U1.3V3, U1.Vin
  SCL: Squix1.SCL, R12.Pin_0, U1.D1
  SDA: Squix1.SCA, R13.Pin_0, U1.D0
  NTC3: MCP1.Chan_4, C1.+, R1.Pin_1
  NTC4: MCP1.Chan_5, C2.+, R3.Pin_1
  NTC5: MCP1.Chan_6, C3.+, R5.Pin_1
  NTC6: MCP1.Chan_7, C4.+, R7.Pin_1
  CS: MCP1.CS/SHDN, U1.D8
  MOSI: MCP1.DIN, U1.D7
  MISO: MCP1.DOUT, U1.D6
  SCLK: MCP1.CLK, U1.D5
  N4: U2.LEFT, R1.Pin_0, R2.Pin_1
  CH9: U2.RIGHT
  CH10: U3.RIGHT
  N5: R15.Pin_0, S1.leg1, U1.D2
  N6: R16.Pin_0, S2.leg0, U1.D3

custom parts:
  LM4040: Voltage Regulator Standard 7805 5V regulator. IGO (Input Ground Output). Spark Fun Electronics SKU : COM-00107
  Vertical Resistor: A generic resistor (0.25W)
  NodeMCU V1.0: ESP8266 based NodeMCU
